# Fritzing sketch backpack_circuit (saved by Fritzing 0.9.3b)
breadboards: 1

parts:
  Bauteil1 = Arduino Uno (Rev3)
  Bauteil2 = Triple Axis Accelerometer Breakout - ADXL335
  R3 = PHOTOCELL [package=photocell]
  R4 = Resistor [tolerance=±5% resistance=220 package="2010 [SMD]"]
  R5 = Resistor [tolerance=±5% resistance=150 package=THT]
  R6 = Resistor [tolerance=±5% resistance=150 package=THT]
  R7 = Resistor [tolerance=±5% resistance=150 package=THT]
  LED1 = LED - 5mm [color="Red (633nm)" package="5 mm [THT]"]
  LED2 = LED - 5mm [color="Yellow (595nm)" package="5 mm [THT]"]
  LED3 = LED - 5mm [color="Green (570nm)" package="5 mm [THT]"]
  LED4 = RGB LED (com. cathode, rgb) [package="5 mm [THT]"]
  R8 = Resistor [tolerance=±5% resistance=150 package=THT]
  R9 = Resistor [tolerance=±5% resistance=150 package=THT]
  R10 = Resistor [tolerance=±5% resistance=150 package=THT]
  J1 = Piezo Speaker

nets:
  N1: Bauteil1.A0, R3.P$2, R4.Pin_0
  N2: Bauteil1.A3, Bauteil2.ZOUT
  N3: Bauteil1.A4/SDA, Bauteil2.YOUT
  N4: Bauteil1.A5/SCL, Bauteil2.XOUT
  N5: Bauteil1.D8, R8.Pin_0
  N6: Bauteil1.D9_PWM, R9.Pin_0
  N7: Bauteil1.D10_PWM/SS, R10.Pin_0
  N8: Bauteil1.D13/SCK, J1.pin1
  N9: Bauteil1.D5_PWM, R5.Pin_0
  N10: Bauteil1.D6_PWM, R6.Pin_0
  N11: Bauteil1.D7, R7.Pin_0
  5V: Bauteil1.5V, Bauteil2.VCC, R4.Pin_1
  GND: Bauteil1.GND, Bauteil2.GND, R3.P$1, LED1.cathode, LED2.cathode, LED3.cathode, LED4.common_cathode, J1.pin2
  N12: R5.Pin_1, LED3.anode
  N13: R6.Pin_1, LED2.anode
  N14: R7.Pin_1, LED1.anode
  N15: LED4.red_anode, R10.Pin_1
  N16: LED4.green_anode, R9.Pin_1
  N17: LED4.blue_anode, R8.Pin_1
